# Fritzing sketch PicoShiftRegister (saved by Fritzing 0.9.3b)
breadboards: 1

parts:
  Mod1 = Raspberry Pi Pico W
  U1 = 74HC595 [package="DIP16 [THT]"]  # not connected
  LED1 = LED - 3mm [color="Red (633nm)" package="3 mm [THT]"]
  LED2 = LED - 3mm [color="Red (633nm)" package="3 mm [THT]"]
  LED3 = LED - 3mm [color="Red (633nm)" package="3 mm [THT]"]
  LED4 = LED - 3mm [color="Red (633nm)" package="3 mm [THT]"]
  LED5 = LED - 3mm [color="Red (633nm)" package="3 mm [THT]"]
  LED6 = LED - 3mm [color="Red (633nm)" package="3 mm [THT]"]
  LED7 = LED - 3mm [color="Red (633nm)" package="3 mm [THT]"]
  LED8 = LED - 3mm [color="Red (633nm)" package="3 mm [THT]"]
  R1 = Resistor [tolerance=±10% resistance=330 package="0402 [SMD]"]
  R2 = Resistor [tolerance=±10% resistance=330 package="0402 [SMD]"]
  R3 = Resistor [tolerance=±10% resistance=330 package="0402 [SMD]"]
  R4 = Resistor [tolerance=±10% resistance=330 package="0402 [SMD]"]
  R5 = Resistor [tolerance=±10% resistance=330 package="0402 [SMD]"]
  R6 = Resistor [tolerance=±10% resistance=330 package="0402 [SMD]"]
  R7 = Resistor [tolerance=±10% resistance=330 package="0402 [SMD]"]
  R8 = Resistor [tolerance=±10% resistance=1.5k package="0402 [SMD]"]

nets:
  N1: Mod1.pin_18, Mod1.pin_38, Mod1.pin_42, R1.Pin_1, R2.Pin_1, R3.Pin_1, R4.Pin_1, R5.Pin_1, R6.Pin_1, R7.Pin_1, R8.Pin_1
  N2: LED1.cathode, R1.Pin_0
  N3: LED2.cathode, R2.Pin_0
  N4: LED3.cathode, R3.Pin_0
  N5: LED4.cathode, R4.Pin_0
  N6: LED5.cathode, R5.Pin_0
  N7: LED6.cathode, R6.Pin_0
  N8: LED7.cathode, R7.Pin_0
  N9: LED8.cathode, R8.Pin_0

custom parts:
  Raspberry Pi Pico W: Raspberry Pi Pico W. Based around the RP2040 microcontroller the Pico W is a low cost microcontroller device bringing Raspberry Pi quality, cost, and easy of use to the microcontroller space. The areas marked KEEPOUT in pcb silkscreen should not have traces running through them to avoid shorts on a soldered in module!
